# Fritzing sketch lag tester (saved by Fritzing 0.9.3b)
perfboards: 1

parts:
  Part2 = Arduino Nano (Rev3.0)
  R6 = Photocell (LDR) [package=THT]
  R7 = Resistor [tolerance=±5% resistance=220 package=THT]
  R8 = Resistor [tolerance=±5% resistance=220 package=THT]
  R10 = Photocell (LDR) [package=THT]
  S2 = Pushbutton [package="[THT]"]
  R11 = Resistor [tolerance=±5% resistance=220 package=THT]
  LED1 = LED - 5mm [color="Red (633nm)" package="5 mm [THT]"]
  R12 = Resistor [tolerance=±5% resistance=220 package=THT]

nets:
  N1: Part2.GND, R6.pin_1, R7.Pin_1, R8.Pin_1, R10.pin_0, R11.Pin_1, LED1.cathode
  N2: Part2.5V, S2.Pin_3, S2.Pin_4, R12.Pin_0
  N3: Part2.A2, S2.Pin_1, S2.Pin_2, R11.Pin_0
  N4: Part2.A1, R8.Pin_0, R10.pin_1
  N5: Part2.A0, R6.pin_0, R7.Pin_0
  N6: LED1.anode, R12.Pin_1

// code stored in the sketch: lagtester.ino
// define pins
const int cameraPin = 0;
const int monitorPin = 1;
const int buttonPin = 2;
const int ledPin = 3;

// timing for LED intervals
unsigned long currentMillisLed = 0;
unsigned long startLedTime = 0;
long OnTime = 250;           // milliseconds of on-time
long OffTime = 750;          // milliseconds of off-time

// timings for sensors
unsigned long currentMillisSensor = 0;
unsigned long cameraTime = 0; // stores camera milis
unsigned long monitorTime = 0; // stores monitor milis
unsigned long timeDifference = 0; // stores actual LAG

// initialize sensor ints, set sensitivity
int cameraState = 0;
int cameraMin = 400;
int cameraMax = 450;
int monitorState = 0;
int monitorMin = 300;
int monitorMax = 350;
int buttonState = LOW; // default button value

int debugMode = false; // set debug mode, used to output RAW values to serial
int debugModeLength = 6; // lazy
int debugModeArray[6] = {cameraState,monitorState,buttonState,cameraTime,monitorTime,timeDifference}; // define printed values in debug mode

void setup() {
// set pins modes
  pinMode(cameraPin, INPUT);
  pinMode(monitorPin, INPUT);
  pinMode(buttonPin, INPUT);
  pinMode(ledPin, OUTPUT);

//  open serial port
  Serial.begin(9600);
}

void loop() {
  // read values
  buttonState = digitalRead(buttonPin);
  cameraState = analogRead(cameraPin);
  monitorState = analogRead(monitorPin);
  
  //  run core functions
  keepFlashing();
  measureLag(); 
  if (debugMode) {
    printDebugInfo();
  }
}

// checks button state and operates LED
int keepFlashing() {
  currentMillisLed = millis();
  if ((buttonState == HIGH) && (currentMillisLed - startLedTime >= OnTime)) {
    startLedTime = currentMillisLed;
    digitalWrite(ledPin, LOW);
  }
  else if ((buttonState == HIGH) && (currentMillisLed - startLedTime >= OffTime)) {
    startLedTime = currentMillisLed;
    digitalWrite(ledPin, HIGH);
  }
  else if ((buttonState == LOW) && (ledPin == HIGH)){
    digitalWrite(ledPin, LOW);
  }
}

// measures lag between camera and screen flashes
int measureLag() {
  cameraTime = currentMillisSensor;
  if ((cameraState > cameraMin) && (cameraState < cameraMax) && (buttonState == HIGH)) {
    cameraTime = currentMillisSensor; // set time of camera flash
  } else {
    cameraTime = 0; //  reset if reading missed
  }

  if ((monitorState > monitorMin) && (monitorState < monitorMax) && (buttonState == HIGH)) {
    monitorTime == currentMillisSensor; // set time of monitor flash
  } else {
    monitorTime = 0; //reset if reading missed
  }
  
  timeDifference = cameraTime - monitorTime;
  if ((timeDifference = 0) ||  (timeDifference < 500)) {
    Serial.print(timeDifference);
  } else if (debugMode) {
    Serial.print("At least one reading missed");
    Serial.print("/t");
  }
};

// sends sensor information to Serial. Order of values defined in debugModeArray
int printDebugInfo() {
  for (int i = 0; i <= debugModeLength; i = i++) {
    Serial.print( debugModeArray[i] );
    Serial.print("\t");
  }

}
